// Logisim project multiplier_2x2.circ as structural Verilog: 2 circuits, main circuit multiper2x2
module multiper2x2 (
  input  a1,
  input  a0,
  input  b1,
  input  bo,
  output p0,
  output p1,
  output p2,
  output p3
);

  wire a0b1_out, a1b1_out, a1bo_out, half_adder_1_carry;

  and a0b0 (p0, a0, bo);
  and a1bo (a1bo_out, a1, bo);
  and a0b1 (a0b1_out, a0, b1);
  and a1b1 (a1b1_out, a1, b1);
  Half_adder half_adder_1 (.a(a1bo_out), .b(a0b1_out), .sum(p1), .carry(half_adder_1_carry));
  Half_adder half_adder_2 (.a(half_adder_1_carry), .b(a1b1_out), .sum(p2), .carry(p3));
endmodule

module Half_adder (
  input  a,
  input  b,
  output sum,
  output carry
);

  xor xor_1 (sum, a, b);
  and and_1 (carry, b, a);
endmodule
